// Logisim project 755232-multi.circ as structural Verilog: 3 circuits, main circuit PROC
module BR4 (
  input  regWrite,
  input  [1:0] RA,
  input  [1:0] RB,
  input  RESET,
  input  CLK,
  input  [1:0] RW,
  input  [31:0] busW,
  output [31:0] busA,
  output [31:0] busB
);

  wire and_1_out, and_2_out, and_3_out, and_4_out, decoder_1_out0, decoder_1_out1, decoder_1_out2,
       decoder_1_out3;
  wire [31:0] register_1_q, register_2_q, register_3_q, register_4_q;

  Decoder #(.select(2), .enable("false")) decoder_1 (
    .out0(decoder_1_out0), .out1(decoder_1_out1), .out2(decoder_1_out2), .out3(decoder_1_out3), .sel(RW));
  and and_1 (and_1_out, decoder_1_out0, regWrite);
  and and_2 (and_2_out, decoder_1_out1, regWrite);
  and and_3 (and_3_out, decoder_1_out2, regWrite);
  and and_4 (and_4_out, decoder_1_out3, regWrite);
  Register #(.width(32)) register_1 (.D(busW), .en(and_1_out), .Q(register_1_q), .clk(CLK), .clr(RESET));
  Register #(.width(32)) register_2 (.D(busW), .en(and_2_out), .Q(register_2_q), .clk(CLK), .clr(RESET));
  Register #(.width(32)) register_3 (.D(busW), .en(and_3_out), .Q(register_3_q), .clk(CLK), .clr(RESET));
  Register #(.width(32)) register_4 (.D(busW), .en(and_4_out), .Q(register_4_q), .clk(CLK), .clr(RESET));
  Multiplexer #(.select(2), .width(32), .enable("false")) multiplexer_1 (
    .in0(register_1_q), .in1(register_2_q), .in2(register_3_q), .in3(register_4_q), .out(busA), .sel(RA));
  Multiplexer #(.select(2), .width(32), .enable("false")) multiplexer_2 (
    .in0(register_1_q), .in1(register_2_q), .in2(register_3_q), .in3(register_4_q), .out(busB), .sel(RB));
endmodule

module BR32 (
  input  regWrite,
  input  reset,
  input  CLK,
  input  [4:0] RA,
  input  [4:0] RB,
  input  [4:0] RW,
  input  [31:0] busW,
  output [31:0] busA,
  output [31:0] busB
);

  wire and_1_out, and_2_out, and_3_out, and_4_out, and_5_out, and_6_out, and_7_out, and_8_out,
       decoder_1_out0, decoder_1_out1, decoder_1_out2, decoder_1_out3, decoder_1_out4, decoder_1_out5,
       decoder_1_out6, decoder_1_out7;
  wire [31:0] br4_1_busa, br4_1_busb, br4_2_busa, br4_2_busb, br4_3_busa, br4_3_busb, br4_4_busa, br4_4_busb,
       br4_5_busa, br4_5_busb, br4_6_busa, br4_6_busb, br4_7_busa, br4_7_busb, br4_8_busa, br4_8_busb;

  and and_1 (and_1_out, regWrite, decoder_1_out0);
  Decoder #(.select(3), .enable("false")) decoder_1 (
    .out0(decoder_1_out0), .out1(decoder_1_out1), .out2(decoder_1_out2), .out3(decoder_1_out3),
    .out4(decoder_1_out4), .out5(decoder_1_out5), .out6(decoder_1_out6), .out7(decoder_1_out7), .sel(RW[4:2]));
  and and_2 (and_2_out, decoder_1_out1, regWrite);
  and and_3 (and_3_out, regWrite, decoder_1_out2);
  and and_4 (and_4_out, decoder_1_out5, regWrite);
  and and_5 (and_5_out, decoder_1_out6, regWrite);
  and and_6 (and_6_out, regWrite, decoder_1_out7);
  and and_7 (and_7_out, decoder_1_out3, regWrite);
  and and_8 (and_8_out, decoder_1_out4, regWrite);
  BR4 br4_1 (
    .regWrite(and_1_out), .RESET(reset), .RW(RW[1:0]), .CLK(CLK), .busW(busW), .busA(br4_1_busa),
    .busB(br4_1_busb), .RA(RA[1:0]), .RB(RB[1:0]));
  BR4 br4_2 (
    .regWrite(and_2_out), .RESET(reset), .RW(RW[1:0]), .CLK(CLK), .busW(busW), .busA(br4_2_busa),
    .busB(br4_2_busb), .RA(RA[1:0]), .RB(RB[1:0]));
  BR4 br4_3 (
    .regWrite(and_3_out), .RESET(reset), .RW(RW[1:0]), .CLK(CLK), .busW(busW), .busA(br4_3_busa),
    .busB(br4_3_busb), .RA(RA[1:0]), .RB(RB[1:0]));
  BR4 br4_4 (
    .regWrite(and_7_out), .RESET(reset), .RW(RW[1:0]), .CLK(CLK), .busW(busW), .busA(br4_4_busa),
    .busB(br4_4_busb), .RA(RA[1:0]), .RB(RB[1:0]));
  BR4 br4_5 (
    .regWrite(and_8_out), .RESET(reset), .RW(RW[1:0]), .CLK(CLK), .busW(busW), .busA(br4_5_busa),
    .busB(br4_5_busb), .RA(RA[1:0]), .RB(RB[1:0]));
  BR4 br4_6 (
    .regWrite(and_4_out), .RESET(reset), .RW(RW[1:0]), .CLK(CLK), .busW(busW), .busA(br4_6_busa),
    .busB(br4_6_busb), .RA(RA[1:0]), .RB(RB[1:0]));
  BR4 br4_7 (
    .regWrite(and_5_out), .RESET(reset), .RW(RW[1:0]), .CLK(CLK), .busW(busW), .busA(br4_7_busa),
    .busB(br4_7_busb), .RA(RA[1:0]), .RB(RB[1:0]));
  BR4 br4_8 (
    .regWrite(and_6_out), .RESET(reset), .RW(RW[1:0]), .CLK(CLK), .busW(busW), .busA(br4_8_busa),
    .busB(br4_8_busb), .RA(RA[1:0]), .RB(RB[1:0]));
  Multiplexer #(.select(3), .width(32), .enable("false")) multiplexer_1 (
    .in0(br4_1_busa), .in1(br4_2_busa), .in2(br4_3_busa), .in3(br4_4_busa), .in4(br4_5_busa),
    .in5(br4_6_busa), .in6(br4_7_busa), .in7(br4_8_busa), .out(busA), .sel(RA[4:2]));
  Multiplexer #(.select(3), .width(32), .enable("false")) multiplexer_2 (
    .in0(br4_1_busb), .in1(br4_2_busb), .in2(br4_3_busb), .in3(br4_4_busb), .in4(br4_5_busb),
    .in5(br4_6_busb), .in6(br4_7_busb), .in7(br4_8_busb), .out(busB), .sel(RB[4:2]));

  // Other names for the same wires on the sheet: RA0_1[1:0] = RA[1:0]; RA2_4[2:0] = RA[4:2]; RB0_1[1:0] = RB[1:0];
  //   RB2_4[2:0] = RB[4:2]; RW0_1[1:0] = RW[1:0]; RW2_4[2:0] = RW[4:2]
endmodule

module PROC (
  input  in_1
);

  wire clk, Co, count, mux, regWrite, writeA, writeB, writeC;
  wire [2:0] register_1_q, rom_2_data;
  wire [4:0] ra, rb, rd;
  wire [5:0] rom_1_data;
  wire [7:0] counter_1_q;
  wire [31:0] adder_1_out, BR32_busa, BR32_busb, K, multiplexer_1_out, RA_q, RB_q, RC_q;

  Clock clock_1 (.out(clk));
  Counter #(.max('ha)) counter_1 (
    .load(1'b0), .D(counter_1_q), .count(count), .Q(counter_1_q), .clk(clk), .clr(in_1));  // open: carry
  Register #(.width(3)) register_1 (.D(rom_2_data), .Q(register_1_q), .clk(clk), .clr(in_1));  // open: en
  ROM #(.dataWidth(22)) rom_1 (.addr(counter_1_q), .data({Co, rd, ra, rb, rom_1_data}));  // open: sel
  ROM #(.addrWidth(4), .dataWidth(3)) rom_2 (.addr({register_1_q, Co}), .data(rom_2_data));  // open: sel
  ROM #(.addrWidth(3), .dataWidth(6)) rom_3 (
    .addr(register_1_q), .data({mux, regWrite, writeA, writeB, writeC, count}));  // open: sel
  assign K = {{16{1'b0}}, {ra, rb, rom_1_data}};  // Bit_Extender bit_extender_1
  Multiplexer #(.width(32), .enable("false")) multiplexer_1 (.in0(K), .in1(RC_q), .out(multiplexer_1_out), .sel(mux));
  BR32 BR32 (
    .regWrite(regWrite), .reset(in_1), .CLK(clk), .RA(ra), .RB(rb), .RW(rd), .busW(multiplexer_1_out),
    .busA(BR32_busa), .busB(BR32_busb));
  Register #(.width(32)) u_RA (.D(BR32_busa), .en(writeA), .Q(RA_q), .clk(clk), .clr(in_1));
  Register #(.width(32)) u_RB (.D(BR32_busb), .en(writeB), .Q(RB_q), .clk(clk), .clr(in_1));
  Adder #(.width(32)) adder_1 (.a(RA_q), .b(RB_q), .out(adder_1_out));  // open: cin, cout
  Register #(.width(32)) RC (.D(adder_1_out), .en(writeC), .Q(RC_q), .clk(clk), .clr(in_1));

  // Other names for the same wires on the sheet: reset = in_1

  // Notes on the sheet:
  //   señal control count
  //   estado
  //   unidad de control (cableada 5 estados)
  //   Unidad de proceso multiciclo (ruta de datos)
  //   contents of rom_1 (hex, n*v repeats v):
  //   7 10005 20005 30002 40003 50002 260040 263080 2630c0 263100 263140
  //   co
  //   rd
  //   ra
  //   rb
  //   K
  //   contents of rom_2 (hex, n*v repeats v):
  //   1 2 0 0 3 3 4 4
  //   contents of rom_3 (hex, n*v repeats v):
  //   0 11 c 2 31
  //   señal control mux
  //   señal control regWrite
  //   señal control writeA
  //   señal control writeB
  //   señal control writeC
endmodule
