// Logisim project 755232-multi2.circ as structural Verilog: 3 circuits, main circuit PROC
module BR4 (
  input  regWrite,
  input  [1:0] RA,
  input  [1:0] RB,
  input  RESET,
  input  CLK,
  input  [1:0] RW,
  input  [31:0] busW,
  output [31:0] busA,
  output [31:0] busB
);

  wire and_1_out, and_2_out, and_3_out, and_4_out, decoder_1_out0, decoder_1_out1, decoder_1_out2,
       decoder_1_out3;
  wire [31:0] register_1_q, register_2_q, register_3_q, register_4_q;

  Decoder #(.select(2), .enable("false")) decoder_1 (
    .out0(decoder_1_out0), .out1(decoder_1_out1), .out2(decoder_1_out2), .out3(decoder_1_out3), .sel(RW));
  and and_1 (and_1_out, decoder_1_out0, regWrite);
  and and_2 (and_2_out, decoder_1_out1, regWrite);
  and and_3 (and_3_out, decoder_1_out2, regWrite);
  and and_4 (and_4_out, decoder_1_out3, regWrite);
  Register #(.width(32)) register_1 (.D(busW), .en(and_1_out), .Q(register_1_q), .clk(CLK), .clr(RESET));
  Register #(.width(32)) register_2 (.D(busW), .en(and_2_out), .Q(register_2_q), .clk(CLK), .clr(RESET));
  Register #(.width(32)) register_3 (.D(busW), .en(and_3_out), .Q(register_3_q), .clk(CLK), .clr(RESET));
  Register #(.width(32)) register_4 (.D(busW), .en(and_4_out), .Q(register_4_q), .clk(CLK), .clr(RESET));
  Multiplexer #(.select(2), .width(32), .enable("false")) multiplexer_1 (
    .in0(register_1_q), .in1(register_2_q), .in2(register_3_q), .in3(register_4_q), .out(busA), .sel(RA));
  Multiplexer #(.select(2), .width(32), .enable("false")) multiplexer_2 (
    .in0(register_1_q), .in1(register_2_q), .in2(register_3_q), .in3(register_4_q), .out(busB), .sel(RB));
endmodule

module BR32 (
  input  regWrite,
  input  reset,
  input  CLK,
  input  [4:0] RA,
  input  [4:0] RB,
  input  [4:0] RW,
  input  [31:0] busW,
  output [31:0] busA,
  output [31:0] busB
);

  wire and_1_out, and_2_out, and_3_out, and_4_out, and_5_out, and_6_out, and_7_out, and_8_out,
       decoder_1_out0, decoder_1_out1, decoder_1_out2, decoder_1_out3, decoder_1_out4, decoder_1_out5,
       decoder_1_out6, decoder_1_out7;
  wire [31:0] br4_1_busa, br4_1_busb, br4_2_busa, br4_2_busb, br4_3_busa, br4_3_busb, br4_4_busa, br4_4_busb,
       br4_5_busa, br4_5_busb, br4_6_busa, br4_6_busb, br4_7_busa, br4_7_busb, br4_8_busa, br4_8_busb;

  and and_1 (and_1_out, regWrite, decoder_1_out0);
  Decoder #(.select(3), .enable("false")) decoder_1 (
    .out0(decoder_1_out0), .out1(decoder_1_out1), .out2(decoder_1_out2), .out3(decoder_1_out3),
    .out4(decoder_1_out4), .out5(decoder_1_out5), .out6(decoder_1_out6), .out7(decoder_1_out7), .sel(RW[4:2]));
  and and_2 (and_2_out, decoder_1_out1, regWrite);
  and and_3 (and_3_out, regWrite, decoder_1_out2);
  and and_4 (and_4_out, decoder_1_out5, regWrite);
  and and_5 (and_5_out, decoder_1_out6, regWrite);
  and and_6 (and_6_out, regWrite, decoder_1_out7);
  and and_7 (and_7_out, decoder_1_out3, regWrite);
  and and_8 (and_8_out, decoder_1_out4, regWrite);
  BR4 br4_1 (
    .regWrite(and_1_out), .RESET(reset), .RW(RW[1:0]), .CLK(CLK), .busW(busW), .busA(br4_1_busa),
    .busB(br4_1_busb), .RA(RA[1:0]), .RB(RB[1:0]));
  BR4 br4_2 (
    .regWrite(and_2_out), .RESET(reset), .RW(RW[1:0]), .CLK(CLK), .busW(busW), .busA(br4_2_busa),
    .busB(br4_2_busb), .RA(RA[1:0]), .RB(RB[1:0]));
  BR4 br4_3 (
    .regWrite(and_3_out), .RESET(reset), .RW(RW[1:0]), .CLK(CLK), .busW(busW), .busA(br4_3_busa),
    .busB(br4_3_busb), .RA(RA[1:0]), .RB(RB[1:0]));
  BR4 br4_4 (
    .regWrite(and_7_out), .RESET(reset), .RW(RW[1:0]), .CLK(CLK), .busW(busW), .busA(br4_4_busa),
    .busB(br4_4_busb), .RA(RA[1:0]), .RB(RB[1:0]));
  BR4 br4_5 (
    .regWrite(and_8_out), .RESET(reset), .RW(RW[1:0]), .CLK(CLK), .busW(busW), .busA(br4_5_busa),
    .busB(br4_5_busb), .RA(RA[1:0]), .RB(RB[1:0]));
  BR4 br4_6 (
    .regWrite(and_4_out), .RESET(reset), .RW(RW[1:0]), .CLK(CLK), .busW(busW), .busA(br4_6_busa),
    .busB(br4_6_busb), .RA(RA[1:0]), .RB(RB[1:0]));
  BR4 br4_7 (
    .regWrite(and_5_out), .RESET(reset), .RW(RW[1:0]), .CLK(CLK), .busW(busW), .busA(br4_7_busa),
    .busB(br4_7_busb), .RA(RA[1:0]), .RB(RB[1:0]));
  BR4 br4_8 (
    .regWrite(and_6_out), .RESET(reset), .RW(RW[1:0]), .CLK(CLK), .busW(busW), .busA(br4_8_busa),
    .busB(br4_8_busb), .RA(RA[1:0]), .RB(RB[1:0]));
  Multiplexer #(.select(3), .width(32), .enable("false")) multiplexer_1 (
    .in0(br4_1_busa), .in1(br4_2_busa), .in2(br4_3_busa), .in3(br4_4_busa), .in4(br4_5_busa),
    .in5(br4_6_busa), .in6(br4_7_busa), .in7(br4_8_busa), .out(busA), .sel(RA[4:2]));
  Multiplexer #(.select(3), .width(32), .enable("false")) multiplexer_2 (
    .in0(br4_1_busb), .in1(br4_2_busb), .in2(br4_3_busb), .in3(br4_4_busb), .in4(br4_5_busb),
    .in5(br4_6_busb), .in6(br4_7_busb), .in7(br4_8_busb), .out(busB), .sel(RB[4:2]));

  // Other names for the same wires on the sheet: RA0_1[1:0] = RA[1:0]; RA2_4[2:0] = RA[4:2]; RB0_1[1:0] = RB[1:0];
  //   RB2_4[2:0] = RB[4:2]; RW0_1[1:0] = RW[1:0]; RW2_4[2:0] = RW[4:2]
endmodule

module PROC (
  input  in_1
);

  wire clk, count0, count1, memR_W, not_1_out, PCwrite, regDst, regWrite, writeA, writeB, writeC, writeIR,
       writeMDR, z;
  wire [1:0] memToReg;
  wire [2:0] Co;
  wire [3:0] register_1_q, rom_2_data;
  wire [4:0] multiplexer_2_out, ra, rb, rd;
  wire [6:0] D6_0;
  wire [10:0] IR_q;
  wire [15:0] A, counter_1_q, multiplexer_1_out;
  wire [28:0] rom_1_data;
  wire [31:0] adder_1_out, BR32_busa, BR32_busb, K, MDR_q, multiplexer_3_out, ram_1_data, RC_q;
  wire [31:7] RB_q;
  wire [31:16] RA_q;

  Counter #(.width(16), .max('hffff)) counter_1 (
    .load(count1), .D(multiplexer_1_out), .count(count0), .Q(counter_1_q), .clk(clk), .clr(in_1));  // open: carry
  Multiplexer #(.width(16), .enable("false")) multiplexer_1 (
    .in0(counter_1_q), .in1({rd, IR_q}), .out(multiplexer_1_out), .sel(PCwrite));
  Clock clock_1 (.out(clk));
  Register #(.width(4)) register_1 (.D(rom_2_data), .Q(register_1_q), .clk(clk), .clr(in_1));  // open: en
  Register #(.width(29)) IR (.D(rom_1_data), .en(writeIR), .Q({Co, ra, rb, rd, IR_q}), .clk(clk), .clr(in_1));
  ROM #(.addrWidth(16), .dataWidth(29)) rom_1 (.addr(counter_1_q), .data(rom_1_data));  // open: sel
  assign K = {{16{1'b0}}, {rd, IR_q}};  // Bit_Extender bit_extender_1
  ROM #(.dataWidth(4)) rom_2 (.addr({register_1_q, Co, z}), .data(rom_2_data));  // open: sel
  ROM #(.addrWidth(4), .dataWidth(13)) rom_3 (
    .addr(register_1_q),
    .data({count1, count0, writeC, writeB, writeA, regWrite, memToReg, regDst, memR_W, writeMDR, PCwrite, writeIR}));  // open: sel
  Multiplexer #(.width(5), .enable("false")) multiplexer_2 (.in0(rb), .in1(rd), .out(multiplexer_2_out), .sel(regDst));
  BR32 BR32 (
    .regWrite(regWrite), .reset(in_1), .CLK(clk), .RA(ra), .RB(rb), .RW(multiplexer_2_out),
    .busW(multiplexer_3_out), .busA(BR32_busa), .busB(BR32_busb));
  Multiplexer #(.select(2), .width(32), .enable("false")) multiplexer_3 (
    .in0(K), .in1(MDR_q), .in2(RC_q), .out(multiplexer_3_out), .sel(memToReg));  // open: in3
  Register #(.width(32)) u_RA (.D(BR32_busa), .en(writeA), .Q({RA_q, A}), .clk(clk), .clr(in_1));
  Register #(.width(32)) u_RB (.D(BR32_busb), .en(writeB), .Q({RB_q, D6_0}), .clk(clk), .clr(in_1));
  Adder #(.width(32)) adder_1 (.a({RA_q, A}), .b({RB_q, D6_0}), .out(adder_1_out));  // open: cin, cout
  Comparator #(.width(32)) comparator_1 (.a(BR32_busa), .b(BR32_busb), .eq(z));  // open: gt, lt
  // tty_ctrl tty_ctrl_1: pin names not known
  // TTY tty_1: pin names not known; wires that end beside it: A, memR_W, D6_0, clk
  Register #(.width(32)) RC (.D(adder_1_out), .en(writeC), .Q(RC_q), .clk(clk), .clr(in_1));
  Register #(.width(32)) MDR (.D(ram_1_data), .en(writeMDR), .Q(MDR_q), .clk(clk), .clr(in_1));
  RAM #(.addrWidth(16), .dataWidth(32), .bus("separate")) ram_1 (
    .addr(A), .din({RB_q, D6_0}), .data(ram_1_data), .str(memR_W), .clk(clk), .ld(not_1_out), .clr(in_1));  // open: sel
  not not_1 (not_1_out, memR_W);

  // Other names for the same wires on the sheet: reset = in_1

  // Notes on the sheet:
  //   señal control count
  //   señal control PCwrite
  //   estado
  //   unidad de control (cableada 5 estados)
  //   Unidad de proceso multiciclo (ruta de datos)
  //   contents of rom_1 (hex, n*v repeats v):
  //   0 10001 20000 30000 40006 50021 1064000c 8a60000 4c21000 4252800 4231800 10210006 c020000 90018
  //   7ffff 10490016 8004e ce80000 8004f ce80000 80020 ce80000 8004f ce80000 8004b ce80000
  //   K
  //   señal control regDst
  //   contents of rom_2 (hex, n*v repeats v):
  //   16*1 2 2 3 3 6 6 9 9 b b 22*0 16*4 16*5 16*0 16*7 16*8 16*0 16*a 17*0 c 0 c 0 c 0 c 0 c 0 c 0 c 0 c
  //   16*d 16*1
  //   contents of rom_3 (hex, n*v repeats v):
  //   801 0 80 300 400 d0 100 4 a0 300 8 300 1002 1
  //   señal control regWrite
  //   señal control memToReg
  //   permiso imprimir
  //   señal control writeA
  //   señal control writeB
  //   señal control writeC
  //   señal control writeMDR
  //   memR/W=1 escribe
  //   memR/W= 0 lee
  //   señal control memR/W
endmodule
