// Logisim project 755232-seg.circ as structural Verilog: 3 circuits, main circuit PROC
module BR4 (
  input  regWrite,
  input  [1:0] RA,
  input  [1:0] RB,
  input  RESET,
  input  CLK,
  input  [1:0] RW,
  input  [31:0] busW,
  output [31:0] busA,
  output [31:0] busB
);

  wire and_1_out, and_2_out, and_3_out, and_4_out, decoder_1_out0, decoder_1_out1, decoder_1_out2,
       decoder_1_out3;
  wire [31:0] register_1_q, register_2_q, register_3_q, register_4_q;

  Decoder #(.select(2), .enable("false")) decoder_1 (
    .out0(decoder_1_out0), .out1(decoder_1_out1), .out2(decoder_1_out2), .out3(decoder_1_out3), .sel(RW));
  and and_1 (and_1_out, decoder_1_out0, regWrite);
  and and_2 (and_2_out, decoder_1_out1, regWrite);
  and and_3 (and_3_out, decoder_1_out2, regWrite);
  and and_4 (and_4_out, decoder_1_out3, regWrite);
  Register #(.width(32)) register_1 (.D(busW), .en(and_1_out), .Q(register_1_q), .clk(CLK), .clr(RESET));
  Register #(.width(32)) register_2 (.D(busW), .en(and_2_out), .Q(register_2_q), .clk(CLK), .clr(RESET));
  Register #(.width(32)) register_3 (.D(busW), .en(and_3_out), .Q(register_3_q), .clk(CLK), .clr(RESET));
  Register #(.width(32)) register_4 (.D(busW), .en(and_4_out), .Q(register_4_q), .clk(CLK), .clr(RESET));
  Multiplexer #(.select(2), .width(32), .enable("false")) multiplexer_1 (
    .in0(register_1_q), .in1(register_2_q), .in2(register_3_q), .in3(register_4_q), .out(busA), .sel(RA));
  Multiplexer #(.select(2), .width(32), .enable("false")) multiplexer_2 (
    .in0(register_1_q), .in1(register_2_q), .in2(register_3_q), .in3(register_4_q), .out(busB), .sel(RB));
endmodule

module BR32 (
  input  regWrite,
  input  reset,
  input  CLK,
  input  [4:0] RA,
  input  [4:0] RB,
  input  [4:0] RW,
  input  [31:0] busW,
  output [31:0] busA,
  output [31:0] busB
);

  wire and_1_out, and_2_out, and_3_out, and_4_out, and_5_out, and_6_out, and_7_out, and_8_out,
       decoder_1_out0, decoder_1_out1, decoder_1_out2, decoder_1_out3, decoder_1_out4, decoder_1_out5,
       decoder_1_out6, decoder_1_out7;
  wire [31:0] br4_1_busa, br4_1_busb, br4_2_busa, br4_2_busb, br4_3_busa, br4_3_busb, br4_4_busa, br4_4_busb,
       br4_5_busa, br4_5_busb, br4_6_busa, br4_6_busb, br4_7_busa, br4_7_busb, br4_8_busa, br4_8_busb;

  and and_1 (and_1_out, regWrite, decoder_1_out0);
  Decoder #(.select(3), .enable("false")) decoder_1 (
    .out0(decoder_1_out0), .out1(decoder_1_out1), .out2(decoder_1_out2), .out3(decoder_1_out3),
    .out4(decoder_1_out4), .out5(decoder_1_out5), .out6(decoder_1_out6), .out7(decoder_1_out7), .sel(RW[4:2]));
  and and_2 (and_2_out, decoder_1_out1, regWrite);
  and and_3 (and_3_out, regWrite, decoder_1_out2);
  and and_4 (and_4_out, decoder_1_out5, regWrite);
  and and_5 (and_5_out, decoder_1_out6, regWrite);
  and and_6 (and_6_out, regWrite, decoder_1_out7);
  and and_7 (and_7_out, decoder_1_out3, regWrite);
  and and_8 (and_8_out, decoder_1_out4, regWrite);
  BR4 br4_1 (
    .regWrite(and_1_out), .RESET(reset), .RW(RW[1:0]), .CLK(CLK), .busW(busW), .busA(br4_1_busa),
    .busB(br4_1_busb), .RA(RA[1:0]), .RB(RB[1:0]));
  BR4 br4_2 (
    .regWrite(and_2_out), .RESET(reset), .RW(RW[1:0]), .CLK(CLK), .busW(busW), .busA(br4_2_busa),
    .busB(br4_2_busb), .RA(RA[1:0]), .RB(RB[1:0]));
  BR4 br4_3 (
    .regWrite(and_3_out), .RESET(reset), .RW(RW[1:0]), .CLK(CLK), .busW(busW), .busA(br4_3_busa),
    .busB(br4_3_busb), .RA(RA[1:0]), .RB(RB[1:0]));
  BR4 br4_4 (
    .regWrite(and_7_out), .RESET(reset), .RW(RW[1:0]), .CLK(CLK), .busW(busW), .busA(br4_4_busa),
    .busB(br4_4_busb), .RA(RA[1:0]), .RB(RB[1:0]));
  BR4 br4_5 (
    .regWrite(and_8_out), .RESET(reset), .RW(RW[1:0]), .CLK(CLK), .busW(busW), .busA(br4_5_busa),
    .busB(br4_5_busb), .RA(RA[1:0]), .RB(RB[1:0]));
  BR4 br4_6 (
    .regWrite(and_4_out), .RESET(reset), .RW(RW[1:0]), .CLK(CLK), .busW(busW), .busA(br4_6_busa),
    .busB(br4_6_busb), .RA(RA[1:0]), .RB(RB[1:0]));
  BR4 br4_7 (
    .regWrite(and_5_out), .RESET(reset), .RW(RW[1:0]), .CLK(CLK), .busW(busW), .busA(br4_7_busa),
    .busB(br4_7_busb), .RA(RA[1:0]), .RB(RB[1:0]));
  BR4 br4_8 (
    .regWrite(and_6_out), .RESET(reset), .RW(RW[1:0]), .CLK(CLK), .busW(busW), .busA(br4_8_busa),
    .busB(br4_8_busb), .RA(RA[1:0]), .RB(RB[1:0]));
  Multiplexer #(.select(3), .width(32), .enable("false")) multiplexer_1 (
    .in0(br4_1_busa), .in1(br4_2_busa), .in2(br4_3_busa), .in3(br4_4_busa), .in4(br4_5_busa),
    .in5(br4_6_busa), .in6(br4_7_busa), .in7(br4_8_busa), .out(busA), .sel(RA[4:2]));
  Multiplexer #(.select(3), .width(32), .enable("false")) multiplexer_2 (
    .in0(br4_1_busb), .in1(br4_2_busb), .in2(br4_3_busb), .in3(br4_4_busb), .in4(br4_5_busb),
    .in5(br4_6_busb), .in6(br4_7_busb), .in7(br4_8_busb), .out(busB), .sel(RB[4:2]));

  // Other names for the same wires on the sheet: RA0_1[1:0] = RA[1:0]; RA2_4[2:0] = RA[4:2]; RB0_1[1:0] = RB[1:0];
  //   RB2_4[2:0] = RB[4:2]; RW0_1[1:0] = RW[1:0]; RW2_4[2:0] = RW[4:2]
endmodule

module PROC (
  input  in_1
);

  wire branch, clk, comparator_1_eq, memR_W, MemWrite_ID_EX_q, not_1_out, RegDst_Ex, RegWrite_EX_MEM_q,
       RegWrite_ID_EX_q, RegWrite_WB, saltar;
  wire [1:0] MemtoReg_EX_MEM_q, MemtoReg_ID_EX_q, MemtoReg_MEM_WB_q;
  wire [4:0] multiplexer_2_out, ra, rb, Reg_Rd_ID_q, Reg_Rt_ID_q, RW_EX_q, RW_WB;
  wire [5:1] rom_2_data;
  wire [6:0] D6_0;
  wire [15:0] A, adder_1_out, K16, multiplexer_1_out, register_1_q;
  wire [28:0] rom_1_data;
  wire [28:26] IR_q;
  wire [31:0] adder_2_out, ALU_out_EX_q, ALU_out_MEM_q, BR32_busa, BR32_busb, busW, inm_ID_2_q, inm_ID_3_q,
       inm_ID_q, K, MDR_q, RA_q, ram_1_data, RB_q;
  wire [31:7] RB_EX_q;
  wire [31:16] RA_EX_q;

  Adder #(.width(16)) adder_1 (.a(16'h1), .b(register_1_q), .out(adder_1_out));  // open: cin, cout
  Register #(.width(16)) register_1 (.D(multiplexer_1_out), .en(1'b1), .Q(register_1_q), .clk(clk), .clr(in_1));
  Clock clock_1 (.out(clk));
  Multiplexer #(.width(16), .enable("false")) multiplexer_1 (
    .in0(adder_1_out), .in1(K16), .out(multiplexer_1_out), .sel(saltar));
  ROM #(.addrWidth(16), .dataWidth(29)) rom_1 (.addr(register_1_q), .data(rom_1_data));  // open: sel
  Register #(.width(29)) IR (.D(rom_1_data), .en(1'b1), .Q({IR_q, ra, rb, K16}), .clk(clk), .clr(in_1));
  assign K = {{16{1'b0}}, K16};  // Bit_Extender bit_extender_1
  Comparator #(.width(32)) comparator_1 (.a(BR32_busa), .b(BR32_busb), .eq(comparator_1_eq));  // open: gt, lt
  ROM #(.addrWidth(3), .dataWidth(6)) rom_2 (.addr(IR_q), .data({rom_2_data, branch}));  // open: sel
  and and_1 (saltar, comparator_1_eq, branch);
  BR32 BR32 (
    .regWrite(RegWrite_WB), .reset(in_1), .CLK(clk), .RA(ra), .RB(rb), .RW(RW_WB), .busW(busW),
    .busA(BR32_busa), .busB(BR32_busb));
  Register #(.width(1)) RegDst_ID_EX (.D(rom_2_data[1]), .en(1'b1), .Q(RegDst_Ex), .clk(clk), .clr(in_1));
  Register #(.width(1)) MemWrite_ID_EX (.D(rom_2_data[2]), .en(1'b1), .Q(MemWrite_ID_EX_q), .clk(clk), .clr(in_1));
  Register #(.width(2)) MemtoReg_ID_EX (.D(rom_2_data[4:3]), .en(1'b1), .Q(MemtoReg_ID_EX_q), .clk(clk), .clr(in_1));
  Register #(.width(1)) RegWrite_ID_EX (.D(rom_2_data[5]), .en(1'b1), .Q(RegWrite_ID_EX_q), .clk(clk), .clr(in_1));
  Register #(.width(32)) u_RA (.D(BR32_busa), .en(1'b1), .Q(RA_q), .clk(clk), .clr(in_1));
  Register #(.width(32)) u_RB (.D(BR32_busb), .en(1'b1), .Q(RB_q), .clk(clk), .clr(in_1));
  Register #(.width(32)) inm_ID (.D(K), .en(1'b1), .Q(inm_ID_q), .clk(clk), .clr(in_1));
  Register #(.width(5)) Reg_Rt_ID (.D(rb), .en(1'b1), .Q(Reg_Rt_ID_q), .clk(clk), .clr(in_1));
  Register #(.width(5)) Reg_Rd_ID (.D(K16[15:11]), .en(1'b1), .Q(Reg_Rd_ID_q), .clk(clk), .clr(in_1));
  Adder #(.width(32)) adder_2 (.a(RA_q), .b(RB_q), .out(adder_2_out));  // open: cin, cout
  Multiplexer #(.width(5), .enable("false")) multiplexer_2 (
    .in0(Reg_Rt_ID_q), .in1(Reg_Rd_ID_q), .out(multiplexer_2_out), .sel(RegDst_Ex));
  // tty_ctrl tty_ctrl_1: pin names not known
  // TTY tty_1: pin names not known; wires that end beside it: A, memR_W, D6_0, clk
  Register #(.width(1)) MemWrite_EX_MEM (.D(MemWrite_ID_EX_q), .en(1'b1), .Q(memR_W), .clk(clk), .clr(in_1));
  Register #(.width(2)) MemtoReg_EX_MEM (.D(MemtoReg_ID_EX_q), .en(1'b1), .Q(MemtoReg_EX_MEM_q), .clk(clk), .clr(in_1));
  Register #(.width(1)) RegWrite_EX_MEM (.D(RegWrite_ID_EX_q), .en(1'b1), .Q(RegWrite_EX_MEM_q), .clk(clk), .clr(in_1));
  Register #(.width(32)) RA_EX (.D(RA_q), .Q({RA_EX_q, A}), .clk(clk), .clr(in_1));  // open: en
  Register #(.width(32)) ALU_out_EX (.D(adder_2_out), .en(1'b1), .Q(ALU_out_EX_q), .clk(clk), .clr(in_1));
  Register #(.width(32)) RB_EX (.D(RB_q), .en(1'b1), .Q({RB_EX_q, D6_0}), .clk(clk), .clr(in_1));
  Register #(.width(32)) inm_ID_2 (.D(inm_ID_q), .en(1'b1), .Q(inm_ID_2_q), .clk(clk), .clr(in_1));
  Register #(.width(5)) RW_EX (.D(multiplexer_2_out), .Q(RW_EX_q), .clk(clk), .clr(in_1));  // open: en
  RAM #(.addrWidth(16), .dataWidth(32), .bus("separate")) ram_1 (
    .addr(A), .din({RB_EX_q, D6_0}), .data(ram_1_data), .str(memR_W), .clk(clk), .ld(not_1_out), .clr(in_1));  // open: sel
  not not_1 (not_1_out, memR_W);
  Register #(.width(2)) MemtoReg_MEM_WB (
    .D(MemtoReg_EX_MEM_q), .en(1'b1), .Q(MemtoReg_MEM_WB_q), .clk(clk), .clr(in_1));
  Register #(.width(1)) RegWrite_MEM_WB (.D(RegWrite_EX_MEM_q), .en(1'b1), .Q(RegWrite_WB), .clk(clk), .clr(in_1));
  Register #(.width(32)) ALU_out_MEM (.D(ALU_out_EX_q), .en(1'b1), .Q(ALU_out_MEM_q), .clk(clk), .clr(in_1));
  Register #(.width(32)) MDR (.D(ram_1_data), .en(1'b1), .Q(MDR_q), .clk(clk), .clr(in_1));
  Register #(.width(32)) inm_ID_3 (.D(inm_ID_2_q), .en(1'b1), .Q(inm_ID_3_q), .clk(clk), .clr(in_1));
  Register #(.width(5)) RW_MEM (.D(RW_EX_q), .Q(RW_WB), .clk(clk), .clr(in_1));  // open: en
  Multiplexer #(.select(2), .width(32), .enable("false")) multiplexer_3 (
    .in0(ALU_out_MEM_q), .in1(MDR_q), .in2(inm_ID_3_q), .out(busW), .sel(MemtoReg_MEM_WB_q));  // open: in3

  // Other names for the same wires on the sheet: rd[4:0] = K16[15:11]; reset = in_1

  // Notes on the sheet:
  //   Unidad de proceso segmentado (ruta de datos)
  //   IF/ID
  //   contents of rom_1 (hex, n*v repeats v):
  //   0 10001 20000 30000 40006 50021 14000000 14000000 10640013 14000000 8a60000 14000000 14000000
  //   14000000 4c21000 4252800 4231800 10210008 14000000 c020000 90018 7ffff 14000000 14000000 10490029
  //   14000000 80004e 14000000 14000000 14000000 ce80000 8004f 14000000 14000000 14000000 ce80000 80020
  //   14000000 14000000 14000000 ce80000 8004f 14000000 14000000 14000000 ce80000 8004b 14000000 14000000
  //   14000000 ce80000
  //   K
  //   unidad de control 
  //   contents of rom_2 (hex, n*v repeats v):
  //   30 22 28 4 1
  //   permiso imprimir
  //   ID/EX
  //   EX/MEM
  //   señal control memR/W
  //   memR/W=1 escribe
  //   memR/W= 0 lee
  //   MEM/WB
endmodule
