// Logisim project 755232-cache.circ as structural Verilog: 1 circuit, main circuit main
module main (
  input  in_1,
  output [31:0] out_2,
  output hit
);

  wire clk, comparator_1_eq, decoder_2_out0, en_R1, en_R2, en_R3, en_R4, load_pc, mem_en, not_1_out,
       not_3_out, not_4_out, not_5_out, not_6_out, not_7_out, not_8_out, not_9_out, not_10_out, not_11_out,
       ram_1_data, way, write, write_via0, write_via1;
  wire [1:0] \byte , word;
  wire [3:0] counter_1_q;
  wire [4:0] set;
  wire [6:0] tag;
  wire [7:0] counter_2_q, ram_2_data, ram_3_data;
  wire [31:0] main_1_dato, multiplexer_1_out, multiplexer_3_out, RAM1, RAM2, RAM3, RAM4, ram_4_data,
       ram_5_data, ram_6_data, ram_7_data, ram_8_data, ram_9_data, ram_10_data, ram_11_data;

  not not_1 (not_1_out, ram_1_data);
  Clock clock_1 (.out(clk));
  RAM #(.addrWidth(5), .dataWidth(1), .bus("separate")) ram_1 (
    .addr(set), .din(not_1_out), .data(ram_1_data), .str(write), .clk(clk), .ld(1'b1), .clr(in_1));  // open: sel
  Decoder #(.disabled(0)) decoder_1 (.out0(write_via0), .out1(write_via1), .sel(ram_1_data), .en(write));
  RAM #(.addrWidth(5), .bus("separate")) ram_2 (
    .addr(set), .din({1'b1, tag}), .data(ram_2_data), .str(write_via0), .clk(clk), .clr(in_1));  // open: sel, ld
  Comparator comparator_1 (.a(ram_2_data), .b({1'b1, tag}), .eq(comparator_1_eq));  // open: gt, lt
  or or_1 (hit, comparator_1_eq, way);
  RAM #(.addrWidth(5), .bus("separate")) ram_3 (
    .addr(set), .din({1'b1, tag}), .data(ram_3_data), .str(write_via1), .clk(clk), .clr(in_1));  // open: sel, ld
  not not_2 (mem_en, hit);
  Comparator comparator_2 (.a(ram_3_data), .b({1'b1, tag}), .eq(way));  // open: gt, lt
  not not_3 (not_3_out, write_via0);
  Counter #(.width(4), .max('hc)) counter_1 (
    .count(not_4_out), .Q(counter_1_q), .clk(clk), .clr(hit));  // open: load, D, carry
  not not_4 (not_4_out, hit);
  RAM #(.addrWidth(5), .dataWidth(32), .bus("separate")) ram_4 (
    .addr(set), .din(RAM1), .data(ram_4_data), .str(write_via0), .clk(clk), .ld(not_3_out), .clr(in_1));  // open: sel
  Decoder #(.select(4), .enable("false")) decoder_2 (
    .out0(decoder_2_out0), .out4(en_R1), .out6(en_R2), .out8(en_R3), .out10(en_R4), .out12(write),
    .sel(counter_1_q));  // open: out1, out2, out3, out5, out7, out9, out11, out13, out14, out15
  RAM #(.addrWidth(5), .dataWidth(32), .bus("separate")) ram_5 (
    .addr(set), .din(RAM2), .data(ram_5_data), .str(write_via0), .clk(clk), .ld(not_5_out), .clr(in_1));  // open: sel
  not not_5 (not_5_out, write_via0);
  and and_1 (load_pc, hit, decoder_2_out0);
  not not_6 (not_6_out, write_via0);
  Multiplexer #(.select(2), .width(32), .enable("false")) multiplexer_1 (
    .in0(ram_4_data), .in1(ram_5_data), .in2(ram_6_data), .in3(ram_7_data), .out(multiplexer_1_out),
    .sel(word));
  RAM #(.addrWidth(5), .dataWidth(32), .bus("separate")) ram_6 (
    .addr(set), .din(RAM3), .data(ram_6_data), .str(write_via0), .clk(clk), .ld(not_6_out), .clr(in_1));  // open: sel
  RAM #(.addrWidth(5), .dataWidth(32), .bus("separate")) ram_7 (
    .addr(set), .din(RAM4), .data(ram_7_data), .str(write_via0), .clk(clk), .ld(not_7_out), .clr(in_1));  // open: sel
  not not_7 (not_7_out, write_via0);
  Register #(.width(32)) register_1 (.D(main_1_dato), .en(en_R1), .Q(RAM1), .clk(clk), .clr(in_1));
  Register #(.width(32)) register_2 (.D(main_1_dato), .en(en_R2), .Q(RAM2), .clk(clk), .clr(in_1));
  MP_main main_1 (.dir({tag, set, word, \byte }), .mem_en(mem_en), .clk(clk), .dato(main_1_dato));
  not not_8 (not_8_out, write_via1);
  Multiplexer #(.width(32), .enable("false")) multiplexer_2 (
    .in0(multiplexer_1_out), .in1(multiplexer_3_out), .out(out_2), .sel(way));
  RAM #(.addrWidth(5), .dataWidth(32), .bus("separate")) ram_8 (
    .addr(set), .din(RAM1), .data(ram_8_data), .str(write_via1), .clk(clk), .ld(not_8_out), .clr(in_1));  // open: sel
  Register #(.width(32)) register_3 (.D(main_1_dato), .en(en_R3), .Q(RAM3), .clk(clk), .clr(in_1));
  Counter counter_2 (.load(1'b0), .count(load_pc), .Q(counter_2_q), .clk(clk), .clr(in_1));  // open: D, carry
  Register #(.width(32)) register_4 (.D(main_1_dato), .en(en_R4), .Q(RAM4), .clk(clk), .clr(in_1));
  not not_9 (not_9_out, write_via1);
  ROM #(.dataWidth(16)) rom_1 (.addr(counter_2_q), .data({tag, set, word, \byte }));  // open: sel
  RAM #(.addrWidth(5), .dataWidth(32), .bus("separate")) ram_9 (
    .addr(set), .din(RAM2), .data(ram_9_data), .str(write_via1), .clk(clk), .ld(not_9_out), .clr(in_1));  // open: sel
  Multiplexer #(.select(2), .width(32), .enable("false")) multiplexer_3 (
    .in0(ram_8_data), .in1(ram_9_data), .in2(ram_10_data), .in3(ram_11_data), .out(multiplexer_3_out),
    .sel(word));
  not not_10 (not_10_out, write_via1);
  RAM #(.addrWidth(5), .dataWidth(32), .bus("separate")) ram_10 (
    .addr(set), .din(RAM3), .data(ram_10_data), .str(write_via1), .clk(clk), .ld(not_10_out), .clr(in_1));  // open: sel
  not not_11 (not_11_out, write_via1);
  RAM #(.addrWidth(5), .dataWidth(32), .bus("separate")) ram_11 (
    .addr(set), .din(RAM4), .data(ram_11_data), .str(write_via1), .clk(clk), .ld(not_11_out), .clr(in_1));  // open: sel

  // Other names for the same wires on the sheet: RAM5[31:0] = RAM1; RAM6[31:0] = RAM2; RAM7[31:0] = RAM3;
  //   RAM8[31:0] = RAM4; reset = in_1

  // Notes on the sheet:
  //   MEMORIA CACHÉ DE INSTRUCIONES, asociativa con 2 vías
  //   GESTIÓN DE ETIQUETAS
  //   RAM1
  //   RAM2
  //   UNIDAD DE CONTROL
  //   RAM3
  //   GESTIÓN DE DATOS
  //   RAM4
  //   RAM5
  //   inst
  //   RAM6
  //   contents of rom_1 (hex, n*v repeats v):
  //   204 408 604 400 894 a98 e94 e90 c808 c204 3608 3600
  //   RAM7
  //   RAM8
endmodule
